// Digital circuit eggtimer.dig as structural Verilog
module eggtimer (
  input  _1_kHz
);

  wire PRESET_out, RST_out, START_out, u_controller_countdown, u_controller_load, u_controller_start,
       u_counter_endd, u_downcounter_zero;
  wire [3:0] dipswitch_1_out, dipswitch_5_out, dipswitch_9_out, dipswitch_13_out, u_downcounter_m1,
       u_downcounter_m10, u_downcounter_s1, u_downcounter_s10;

  Button #(.activeLow("true")) RST (.out(RST_out));
  Seven_Seg_Hex seven_seg_hex_1 (.d(u_downcounter_m10), .dp(1'b0));
  DipSwitch dipswitch_1 (.out(dipswitch_1_out[3]));
  DipSwitch dipswitch_2 (.out(dipswitch_1_out[2]));
  DipSwitch dipswitch_3 (.out(dipswitch_1_out[1]));
  Seven_Seg_Hex seven_seg_hex_2 (.d(u_downcounter_m1), .dp(1'b1));
  downcounter #(.applicationType("IVERILOG")) u_downcounter (
    .rst(RST_out), .c1khz(_1_kHz), .count(u_controller_countdown), .load(u_controller_load),
    .pm10(dipswitch_1_out), .pm1(dipswitch_5_out), .ps10(dipswitch_9_out), .ps1(dipswitch_13_out),
    .m10(u_downcounter_m10), .m1(u_downcounter_m1), .s10(u_downcounter_s10), .s1(u_downcounter_s1),
    .zero(u_downcounter_zero));
  DipSwitch dipswitch_4 (.out(dipswitch_1_out[0]));
  DipSwitch dipswitch_5 (.out(dipswitch_5_out[3]));
  DipSwitch dipswitch_6 (.out(dipswitch_5_out[2]));
  Seven_Seg_Hex seven_seg_hex_3 (.d(u_downcounter_s10), .dp(1'b0));
  DipSwitch dipswitch_7 (.out(dipswitch_5_out[1]));
  DipSwitch dipswitch_8 (.out(dipswitch_5_out[0]));
  DipSwitch dipswitch_9 (.out(dipswitch_9_out[3]));
  Seven_Seg_Hex seven_seg_hex_4 (.d(u_downcounter_s1), .dp(1'b0));
  DipSwitch dipswitch_10 (.out(dipswitch_9_out[2]));
  DipSwitch dipswitch_11 (.out(dipswitch_9_out[1]));
  DipSwitch dipswitch_12 (.out(dipswitch_9_out[0]));
  DipSwitch dipswitch_13 (.out(dipswitch_13_out[3]));
  DipSwitch dipswitch_14 (.out(dipswitch_13_out[2]));
  DipSwitch dipswitch_15 (.out(dipswitch_13_out[1]));
  DipSwitch dipswitch_16 (.out(dipswitch_13_out[0]));
  controller #(.applicationType("IVERILOG")) u_controller (
    .c1khz(_1_kHz), .rst(RST_out), .beginn(START_out), .reset(PRESET_out), .zero(u_downcounter_zero),
    .endd(u_counter_endd), .load(u_controller_load), .start(u_controller_start),
    .countdown(u_controller_countdown));
  Button START (.out(START_out));
  Button PRESET (.out(PRESET_out));
  counter #(.applicationType("IVERILOG")) u_counter (
    .rst(RST_out), .clk(_1_kHz), .start(u_controller_start), .endd(u_counter_endd));

  // Notes on the sheet:
  //   _1_kHz: Hz: 1000
endmodule

/* Code of downcounter:
module downcounter(
  input rst, c1khz,
  input count, load, 
  input [3:0] pm10,
  input [3:0] pm1,
  input [3:0] ps10,
  input [3:0] ps1,
  output reg [3:0] m10,
  output reg [3:0] m1,
  output reg [3:0] s10,
  output reg [3:0] s1,
  output zero);
    
  reg [0:0] zero_r = 1;
  assign zero = (zero_r==1);


    
  reg [3:0]min10;
  reg [3:0]min1;
  reg [3:0]sec10;
  reg [3:0]sec1;
  
  always @(posedge count, negedge rst, posedge load)
    begin
      if (~rst)
        begin
          min10 <= 0;
          min1 <= 0;
          sec10 <= 0;
          sec1 <= 0;
          zero_r <= 1;
        end

      else if (load == 1)
        begin
          if (pm10 > 9)
            begin
              min10 <= 9;
            end
          else
            begin
              min10 <= pm10;
            end
        
          if (pm1 > 9)
            begin
              min1 <= 9;
            end
          else
            begin
              min1 <= pm1;
            end

          if (ps10 > 5)
            begin
              sec10 <= 5;
            end
          else
            begin
              sec10 <= ps10;
            end
        
          if (ps1 > 9)
            begin
              sec1 <= 9;
            end
          else
            begin
              sec1 <= ps1;
            end

          zero_r <= 0;
        end

      else if (count == 1)
        begin
          if (sec1 != 0)
            begin
              sec1 <= sec1 - 1;
              zero_r <= 0;
            end
          else
            begin
              if (sec10 != 0)
                begin
                  sec10 <= sec10 - 1;
                  sec1 <= 9;
                  zero_r <= 0;
                end
              else
                begin
                  if (min1 != 0)
                    begin
                      min1 <= min1 -1;
                      sec10 <= 5;
                      sec1 <= 9;
                      zero_r <= 0;
                    end
                  else
                    begin
                      if (min10 != 0)
                        begin
                          min10 <= min10 - 1;
                          min1 <= 9;
                          sec10 <= 5;
                          sec1 <= 9;
                          zero_r <= 0;
                        end
                      else
                        begin
                          zero_r <= 1;
                        end
                    end
                end
            end
        end       
    end	    

always @(posedge c1khz)
begin     
   m10 <= min10;
   m1 <= min1;
   s10 <= sec10;
   s1 <= sec1;
end

endmodule
*/

/* Code of controller:
module controller(
    input c1khz,
    input rst,
    input beginn, 
    input reset,
    input zero,
    input endd,
    output load,
    output start,
    output countdown
    );

    reg [1:0] state = 2'b00;
  localparam [1:0] // 4 states are required for Moore
    zeroState = 2'b00, // nothing started state
    oneState = 2'b01,  // counter start state
    twoState = 2'b10,  // counter end state
    threeState = 2'b11; // start again state
  

  reg countTemp;
  assign countdown= (endd && ~(state == zeroState));
  reg startTemp;
  assign start = startTemp;
  reg loadTemp;
	


assign load = reset;

always @(posedge c1khz, negedge rst)
begin
  if(~rst)
  begin
  state <= zeroState;
  end
  else if (beginn && ~zero)
  begin
  state <= oneState;
  end
  else if (reset)
  begin
  state <= zeroState;
  end
  else if (zero)
  begin
  state <= zeroState;
  end
  case(state)
	zeroState: // nothing started state
	begin
	countTemp <= 0;
	end
	oneState:
	begin
	startTemp <= 1;

	state <= twoState;
	end
	twoState:
	begin
	startTemp <= 0;
	if (endd)
	state <= oneState;
	end
	threeState:
	begin
	end
     
  endcase



end // always


 
endmodule
*/

/* Code of counter:
`timescale 1ns / 1ps

module counter(
    input rst,
    input clk,
    input start,
    output endd);
    
    reg [9:0] cnt;
    
    assign endd = (cnt==0);
    
    always @(posedge clk, negedge rst)
    begin
        if (~rst)
        begin
            cnt <= 0;
        end
        else
        begin
            if (start)
                cnt <= 999;  // need to check this number
            else if (~endd)
                cnt <= cnt-1;
        end
    end // always
endmodule
*/
